# Fritzing sketch board (saved by Fritzing 0.9.2b)
perfboards: 1

parts:
  S1 = Pushbutton [package="[THT]"]
  S2 = Pushbutton [package="[THT]"]
  S3 = Pushbutton [package="[THT]"]
  LED1 = LED - 5mm [color="Red (633nm)" package="5 mm [THT]"]
  LED2 = LED - 5mm [color="Green (555nm)" package="5 mm [THT]"]
  LED3 = LED - 5mm [color="Blue (470nm)" package="5 mm [THT]"]
  ENCODER1 = Rotary Encoder with Knob
  BUTTON1 = Waterproof Pushbutton (red)
  BUTTON3 = Waterproof Pushbutton (green)
  Part2 = Thumb Joystick
  U1 = SWITCH_SPDT [package=kps-1290]  # not connected
  S4 = Toggle Switch [package=THT]
  S5 = Toggle Switch [package=THT]
  S6 = Toggle Switch [package=THT]
  S7 = Toggle Switch [package=THT]
  LED4 = LED - 5mm [color="White (4500K)" package="5 mm [THT]"]
  R1 = Photocell (LDR) [package=THT]
  NEOPIXEL1 = Neopixel Strip -- White (60/m)  # not connected
  R6 = Resistor [tolerance=±5% resistance=10k package=THT]
  R7 = Resistor [tolerance=±5% resistance=10k package=THT]
  R8 = Resistor [tolerance=±5% resistance=10k package=THT]
  R9 = Resistor [tolerance=±5% resistance=10k package=THT]
  BUTTON2 = Waterproof Pushbutton (blue)
  R4 = Resistor [tolerance=±5% resistance=220k package=THT]
  R2 = Resistor [tolerance=±5% resistance=220k package=THT]
  R5 = Resistor [tolerance=±5% resistance=100k package=THT]
  R3 = Resistor [tolerance=±5% resistance=100k package=THT]
  R10 = Resistor [tolerance=±5% resistance=1k package=THT]
  R11 = Resistor [tolerance=±5% resistance=47 package=THT]
  R12 = Resistor [tolerance=±5% resistance=470 package=THT]
  R13 = Resistor [tolerance=±5% resistance=200 package=THT]
  R14 = Resistor [tolerance=±5% resistance=470 package=THT]  # not connected

nets:
  N1: S1.Pin_3, S1.Pin_4, S2.Pin_3, S2.Pin_4, S3.Pin_3, LED2.anode
  N2: LED1.cathode, R12.Pin_0
  N3: LED2.cathode, R11.Pin_0
  N4: LED3.cathode, R10.Pin_0
  N5: ENCODER1.no_name_yet#1, R8.Pin_1
  N6: ENCODER1.no_name_yet#2, ENCODER1.no_name_yet#4
  N7: ENCODER1.no_name_yet#3, R9.Pin_1
  N8: BUTTON1.no_name_yet#2, BUTTON2.no_name_yet#5
  N9: BUTTON1.no_name_yet#5, BUTTON2.no_name_yet#2
  N10: BUTTON3.no_name_yet#1, R6.Pin_0
  N11: BUTTON3.no_name_yet#2, BUTTON3.no_name_yet#5
  N12: BUTTON3.no_name_yet#4, R7.Pin_0
  N13: Part2.HORZ, R4.Pin_1
  N14: Part2.VERT, R2.Pin_1
  N15: S4.COM, S7.COM
  N16: S5.COM, S6.COM
  N17: LED4.cathode, R13.Pin_1
  N18: R1.pin_0, R8.Pin_0
  N19: R6.Pin_1, R9.Pin_0
  N20: R4.Pin_0, R5.Pin_0
  N21: R2.Pin_0, R3.Pin_0

notes:
  GPIO 34-39 - input only! no pull-up/down!
  GPIO 32-39 - ADC

custom parts:
  Rotary Encoder with Knob: Rotary Encoder with 1/4" Shaft and Knob
  Waterproof Pushbutton (red): Waterproof Illuminated Pushbutton (red)
  Waterproof Pushbutton (green): Waterproof Illuminated Pushbutton (green)
  Neopixel Strip -- White (60/m): Neopixel Strip, White, 60 pixels per meter.
  Waterproof Pushbutton (blue): Waterproof Illuminated Pushbutton (blue)
